# Fritzing sketch eureka (saved by Fritzing 0.8.5b)
breadboards: 1

parts:
  Bauteil2 = Electric Imp Breakout
  LED1 = LED - 3mm [color="White (4500K)" package="3 mm [THT]"]
  VCC1 = 4 x AAA Battery Mount
  S4 = Toggle Switch [package=THT]
  R1 = Resistor [tolerance=±5% resistance=100 package=THT]
  S6 = Pushbutton [package=THT]

nets:
  N1: Bauteil2.1, S6.leg0
  N2: Bauteil2.6, R1.Pin_1
  N3: Bauteil2.8, S6.leg1
  N4: Bauteil2.9, LED1.anode
  N5: Bauteil2.12, S4.L2
  N6: Bauteil2.13, S4.COM
  N7: Bauteil2.14, S4.L1
  N8: Bauteil2.15, VCC1.+
  N9: Bauteil2.16, VCC1.-
  N10: LED1.cathode, R1.Pin_0

custom parts:
  Electric Imp Breakout: Electric Imp Breakout Board with onboard 3.3V regulated power supply
